# Fritzing sketch layoutDynamic (saved by Fritzing 0.9.3b)
breadboards: 1

parts:
  Part1 = Arduino Uno (Rev3)
  R1 = Resistor [tolerance=±5% resistance=10k package="2512 [SMD]"]
  S1 = Pushbutton [package="[SMD]"]
  LED1 = smd LED [color="Green (555nm)" package="0603 [SMD]"]
  LED2 = smd LED [color="Green (555nm)" package="0603 [SMD]"]
  LED3 = smd LED [color="Green (555nm)" package="0603 [SMD]"]
  R2 = Resistor [tolerance=±5% resistance=560 package="2512 [SMD]"]
  R3 = Resistor [tolerance=±5% resistance=560 package="2512 [SMD]"]
  R4 = Resistor [tolerance=±5% resistance=560 package="2512 [SMD]"]
  R5 = Resistor [tolerance=±5% resistance=560 package="2512 [SMD]"]
  LED4 = smd LED [color="White (8000K)" package="0603 [SMD]"]
  J1 = Piezo Speaker

nets:
  N1: Part1.D8, J1.pin2
  N2: Part1.D9_PWM, LED4.anode
  N3: Part1.D2, R1.Pin_0, S1.Pin_1, S1.Pin_2
  N4: Part1.D4, LED2.anode
  N5: Part1.D5_PWM, LED1.anode
  N6: Part1.D6_PWM, LED3.anode
  N7: Part1.5V, R1.Pin_1
  N8: Part1.GND, S1.Pin_3, S1.Pin_4, R2.Pin_0, R3.Pin_0, R4.Pin_0, R5.Pin_0, J1.pin1
  N9: LED1.cathode, R5.Pin_1
  N10: LED2.cathode, R2.Pin_1
  N11: LED3.cathode, R4.Pin_1
  N12: R3.Pin_1, LED4.cathode
