# Fritzing sketch megaLayout (saved by Fritzing 0.9.3b)
breadboards: 1

parts:
  Part1 = Arduino Mega 2560 (Rev3)
  J1 = Piezo Speaker
  R1 = Resistor [tolerance=±5% resistance=560 package="2512 [SMD]"]
  R2 = Resistor [tolerance=±5% resistance=560 package="2512 [SMD]"]
  R3 = Resistor [tolerance=±5% resistance=560 package="2512 [SMD]"]
  R4 = Resistor [tolerance=±5% resistance=560 package="2512 [SMD]"]
  R5 = Resistor [tolerance=±5% resistance=560 package="2512 [SMD]"]
  R6 = Resistor [tolerance=±5% resistance=560 package="2512 [SMD]"]
  R7 = Resistor [tolerance=±5% resistance=560 package="2512 [SMD]"]
  R8 = Resistor [tolerance=±5% resistance=560 package="2512 [SMD]"]
  LED1 = LED - 3mm [color="Green (555nm)" package="3 mm [THT]"]
  LED2 = LED - 3mm [color="Green (555nm)" package="3 mm [THT]"]
  LED4 = LED - 3mm [color="Green (555nm)" package="3 mm [THT]"]
  LED5 = smd LED [color="Red (633nm)" package="0603 [SMD]"]
  LED6 = smd LED [color="White (8000K)" package="0603 [SMD]"]
  LED7 = smd LED [color="Red (633nm)" package="0603 [SMD]"]
  LED8 = smd LED [color="Red (633nm)" package="0603 [SMD]"]
  LED9 = smd LED [color="White (8000K)" package="0603 [SMD]"]
  S1 = Pushbutton [package="[SMD]"]
  S2 = Pushbutton [package="[THT]"]
  R9 = Resistor [tolerance=±5% resistance=10k package="2512 [SMD]"]
  R10 = Resistor [tolerance=±5% resistance=10k package="2512 [SMD]"]
  J2 = Basic Servo
  J3 = Basic Servo
  LED10 = smd LED [color="Red (633nm)" package="0603 [SMD]"]
  R11 = Resistor [tolerance=±5% resistance=560 package="2512 [SMD]"]
  R12 = Resistor [tolerance=±5% resistance=560 package="2512 [SMD]"]
  R13 = Resistor [tolerance=±5% resistance=560 package="2512 [SMD]"]
  R14 = Resistor [tolerance=±5% resistance=560 package="2512 [SMD]"]
  LED12 = smd LED [color="Red (633nm)" package="0603 [SMD]"]
  LED13 = smd LED [color="Red (633nm)" package="0603 [SMD]"]
  LED14 = smd LED [color="White (8000K)" package="0603 [SMD]"]
  S3 = Pushbutton [package="[SMD]"]
  R15 = Resistor [tolerance=±5% resistance=10k package="2512 [SMD]"]
  J4 = Basic Servo

nets:
  VCC: Part1.5V, R9.Pin_0, R10.Pin_0, J2.vcc, J3.vcc, R15.Pin_0, J4.vcc
  GND: Part1.GND, J1.pin1, R1.Pin_0, R2.Pin_0, R3.Pin_0, R4.Pin_0, R5.Pin_0, R6.Pin_0, R7.Pin_0, R8.Pin_0, J2.gnd, J3.gnd, R11.Pin_0, R12.Pin_0, R13.Pin_0, R14.Pin_0
  N1: Part1.D2_PWM, S1.Pin_3, S1.Pin_4
  N2: Part1.D3_PWM, S2.Pin_3, S2.Pin_4
  N3: Part1.D4_PWM, S3.Pin_3, S3.Pin_4
  N4: Part1.D37, LED14.anode
  N5: Part1.D39, LED12.anode
  N6: Part1.D40, J4.pulse
  N7: Part1.D41, LED13.anode
  N8: Part1.D42, J2.pulse
  N9: Part1.D43, LED10.anode
  N10: Part1.D44, J3.pulse
  N11: Part1.D45, J1.pin2
  N12: Part1.D46, LED9.anode
  N13: Part1.D47, LED6.anode
  N14: Part1.D48, LED2.anode
  N15: Part1.D49, LED7.anode
  N16: Part1.D50, LED4.anode
  N17: Part1.D51, LED8.anode
  N18: Part1.D52, LED1.anode
  N19: Part1.D53, LED5.anode
  N20: R1.Pin_1, LED1.cathode
  N21: R2.Pin_1, LED6.cathode
  N22: R3.Pin_1, LED7.cathode
  N23: R4.Pin_1, LED8.cathode
  N24: R5.Pin_1, LED5.cathode
  N25: R6.Pin_1, LED9.cathode
  N26: R7.Pin_1, LED2.cathode
  N27: R8.Pin_1, LED4.cathode
  N28: S1.Pin_1, S1.Pin_2, R9.Pin_1
  N29: S2.Pin_1, S2.Pin_2, R10.Pin_1
  N30: LED10.cathode, R13.Pin_1
  N31: R11.Pin_1, LED14.cathode
  N32: R12.Pin_1, LED12.cathode
  N33: R14.Pin_1, LED13.cathode
  N34: S3.Pin_1, S3.Pin_2, R15.Pin_1
