# Fritzing sketch shiftRegLay (saved by Fritzing 0.9.3b)
breadboards: 1

parts:
  Part1 = Arduino Uno (Rev3)
  LED1 = smd LED [color="Green (555nm)" package="0805 [SMD]"]
  LED2 = smd LED [color="Green (555nm)" package="0805 [SMD]"]
  LED3 = smd LED [color="Green (555nm)" package="0805 [SMD]"]
  R1 = Resistor [tolerance=±5% resistance=560 package="0402 [SMD]"]
  R2 = Resistor [tolerance=±5% resistance=560 package="0402 [SMD]"]
  R3 = Resistor [tolerance=±5% resistance=560 package="0402 [SMD]"]
  R4 = Resistor [tolerance=±5% resistance=560 package="0402 [SMD]"]
  R5 = Resistor [tolerance=±5% resistance=560 package="0402 [SMD]"]
  R6 = Resistor [tolerance=±5% resistance=560 package="0402 [SMD]"]
  R7 = Resistor [tolerance=±5% resistance=560 package="0402 [SMD]"]
  R8 = Resistor [tolerance=±5% resistance=560 package="0402 [SMD]"]
  LED4 = smd LED [color="White (8000K)" package="0805 [SMD]"]
  LED5 = smd LED [color="Red (633nm)" package="0805 [SMD]"]
  LED6 = smd LED [color="Red (633nm)" package="0805 [SMD]"]
  LED7 = smd LED [color="Red (633nm)" package="0805 [SMD]"]
  LED8 = smd LED [color="White (8000K)" package="0805 [SMD]"]
  J1 = Piezo Speaker
  R9 = Rotary Potentiometer (Small) [maximum_resistance=100kΩ package=THT]
  S1 = Momentary Switch [package=ksa_sealed_tac_switch]
  S2 = Momentary Switch [package=ksa_sealed_tac_switch]
  R10 = Resistor [tolerance=±5% resistance=10k package="0402 [SMD]"]
  R11 = Resistor [tolerance=±5% resistance=10k package="0402 [SMD]"]
  U1 = PCF8574 [package="DIP16 [THT]"]
  S3 = Momentary Switch [package=ksa_sealed_tac_switch]
  R12 = Resistor [tolerance=±5% resistance=10k package="0402 [SMD]"]
  LED9 = smd LED [color="White (8000K)" package="0805 [SMD]"]
  R13 = Resistor [tolerance=±5% resistance=560 package="0402 [SMD]"]
  R14 = Resistor [tolerance=±5% resistance=560 package="0402 [SMD]"]
  R15 = Resistor [tolerance=±5% resistance=560 package="0402 [SMD]"]
  R16 = Resistor [tolerance=±5% resistance=560 package="0402 [SMD]"]
  LED10 = smd LED [color="Green (555nm)" package="0805 [SMD]"]
  LED11 = smd LED [color="Green (555nm)" package="0805 [SMD]"]
  LED12 = smd LED [color="Green (555nm)" package="0805 [SMD]"]
  J2 = Basic Servo

nets:
  N1: Part1.D8, U1.P6
  N2: Part1.D9_PWM, U1.P7
  N3: Part1.D10_PWM/SS, U1.SCL
  N4: Part1.D11_PWM/MOSI, J2.pulse
  N5: Part1.D12/MISO, S3.4, R12.Pin_0
  N6: Part1.D13/SCK, J1.pin2
  N7: Part1.D2, S1.4, R10.Pin_0
  N8: Part1.D3_PWM, S2.4, R11.Pin_0
  N9: Part1.D4, LED12.cathode
  N10: Part1.D5_PWM, LED10.cathode
  N11: Part1.D6_PWM, LED11.cathode
  N12: Part1.D7, LED9.cathode
  VCC: Part1.5V, R9.leg2, R10.Pin_1, R11.Pin_1, U1.P5, U1.VCC, R12.Pin_1, J2.vcc
  GND: Part1.GND, R1.Pin_1, R2.Pin_1, R3.Pin_0, R4.Pin_0, R5.Pin_0, R6.Pin_0, R7.Pin_1, R8.Pin_1, J1.pin1, R9.leg1, S1.2, S2.2, U1.GND, U1.INT, R14.Pin_0, R15.Pin_0, J2.gnd
  N13: LED1.cathode, U1.SDA
  N14: LED1.anode, R1.Pin_0
  N15: LED2.cathode, U1.A1
  N16: LED2.anode, R7.Pin_0, LED6.cathode, U1.P2
  N17: LED3.cathode, U1.A0
  N18: LED3.anode, R8.Pin_0
  N19: R2.Pin_0, LED4.anode
  N20: R3.Pin_1, LED8.anode
  N21: R4.Pin_1, LED6.anode
  N22: R5.Pin_1, LED7.anode
  N23: R6.Pin_1, LED5.anode
  N24: LED4.cathode, U1.A3
  N25: LED5.cathode, U1.P0
  N26: LED7.cathode, U1.P1
  N27: LED8.cathode, U1.P3
  N28: S3.1, LED9.anode, R13.Pin_1
  N29: S3.3, R14.Pin_1, LED11.anode
  N30: R15.Pin_1, LED10.anode
  N31: R16.Pin_1, LED12.anode
